// Logisim project 7_Segment_Display.circ as structural Verilog: 1 circuit, main circuit main
module main (
  input  X,
  input  Y,
  input  Z
);

  _7_Segment_Display u_7_segment_display_1 (.g(X));  // open: f, a, b, e, d, c, dp
endmodule
